// Logisim project whyjs.circ as structural Verilog
module ALU (
  input  [11:0] opcode,
  input  [11:0] funct,
  input  [31:0] A_hi,
  input  [31:0] A_lo,
  input  [31:0] B_hi,
  input  [31:0] B_lo,
  output [31:0] Z_hi,
  output [31:0] Z_lo
);

  wire add_c, adder_1_cout, sub_c, subtractor_1_bout;
  wire [4:0] alu_rlogic_ob_selector_1_sel, alu_rmath_ob_selector_1_sel, Z_sel;
  wire [31:0] add_hi, add_lo, sub_hi, sub_lo;

  Adder #(.width(32)) adder_1 (.a(A_lo), .b(B_lo), .out(add_lo), .cout(adder_1_cout));  // open: cin
  Adder #(.width(32)) adder_2 (.a(A_hi), .b(B_hi), .out(add_hi), .cin(adder_1_cout), .cout(add_c));
  Subtractor #(.width(32)) subtractor_1 (.a(A_lo), .b(B_lo), .out(sub_lo), .bout(subtractor_1_bout));  // open: bin
  Subtractor #(.width(32)) subtractor_2 (.a(A_hi), .b(B_hi), .out(sub_hi), .bin(subtractor_1_bout), .bout(sub_c));
  ALU__RMath_OB_Selector alu_rmath_ob_selector_1 (.opcode(opcode), .funct(funct), .sel(alu_rmath_ob_selector_1_sel));
  ALU__RLogic_OB_Selector alu_rlogic_ob_selector_1 (.opcode(opcode), .funct(funct), .sel(alu_rlogic_ob_selector_1_sel));
  assign Z_sel = alu_rmath_ob_selector_1_sel | alu_rlogic_ob_selector_1_sel;  // OR_Gate or_1, 5 bits wide
  Multiplexer #(.select(4)) multiplexer_1 ();  // open: in0, in1, in2, in3, in4, in5, in6, in7, in8, in9, in10, in11, in12, in13, in14, in15, out, sel, en
  Double_Cmp_12_32 double_cmp_12_32_1 (.A(opcode), .B(funct), .X(12'h1), .Y({12{1'b0}}));  // open: Z
  Double_Cmp_12_32 double_cmp_12_32_2 (.A(opcode), .B(funct), .X(12'h1), .Y(12'h1));  // open: Z
  Double_Cmp_12_32 double_cmp_12_32_3 (.A(opcode), .B(funct), .X(12'h1), .Y(12'h2));  // open: Z
  Double_Cmp_12_32 double_cmp_12_32_4 (.A(opcode), .B(funct), .X(12'h1), .Y(12'h2));  // open: Z
  Double_Cmp_12_32 double_cmp_12_32_5 (.A(opcode), .B(funct), .X(12'h1), .Y(12'h3));  // open: Z
  Double_Cmp_12_32 double_cmp_12_32_6 (.A(opcode), .B(funct), .X(12'h1), .Y(12'h4));  // open: Z
  Double_Cmp_12_32 double_cmp_12_32_7 (.A(opcode), .B(funct), .X(12'h1), .Y(12'h5));  // open: Z
  Double_Cmp_12_32 double_cmp_12_32_8 (.A(opcode), .B(funct), .X(12'h1), .Y(12'h6));  // open: Z
  Double_Cmp_12_32 double_cmp_12_32_9 (.A(opcode), .B(funct), .X(12'h1), .Y(12'h7));  // open: Z
  Double_Cmp_12_32 double_cmp_12_32_10 (.A(opcode), .B(funct), .X(12'h1), .Y(12'h8));  // open: Z
  Double_Cmp_12_32 double_cmp_12_32_11 (.A(opcode), .B(funct), .X(funct), .Y(12'h9));  // open: Z
endmodule

module ALU__RMath_OB_Selector (
  input  [11:0] opcode,
  input  [11:0] funct,
  output [4:0] sel
);

  wire comparator_1_eq;
  wire [4:0] and_1_out, and_2_out, and_3_out, and_4_out, and_5_out, and_6_out, and_7_out, and_8_out,
       bit_extender_1_out, constant_cmp_12_5_1_z, constant_cmp_12_5_2_z, constant_cmp_12_5_3_z,
       constant_cmp_12_5_4_z, constant_cmp_12_5_5_z, constant_cmp_12_5_6_z, constant_cmp_12_5_7_z,
       constant_cmp_12_5_8_z, or_1_out, or_3_out;

  Comparator #(.width(12)) comparator_1 (.a(opcode), .b(12'h1), .eq(comparator_1_eq));  // open: gt, lt
  assign bit_extender_1_out = {{4{comparator_1_eq}}, comparator_1_eq};  // Bit_Extender bit_extender_1
  Constant_Cmp_12_5 constant_cmp_12_5_1 (.A(funct), .B({12{1'b0}}), .Z(constant_cmp_12_5_1_z), .outconst({5{1'b0}}));
  Constant_Cmp_12_5 constant_cmp_12_5_2 (.A(funct), .B(12'h1), .Z(constant_cmp_12_5_2_z), .outconst(5'b00001));
  Constant_Cmp_12_5 constant_cmp_12_5_3 (.A(funct), .B(12'h2), .Z(constant_cmp_12_5_3_z), .outconst(5'b00010));
  Constant_Cmp_12_5 constant_cmp_12_5_4 (.A(funct), .B(12'h5), .Z(constant_cmp_12_5_4_z), .outconst(5'b00011));
  Constant_Cmp_12_5 constant_cmp_12_5_5 (.A(funct), .B(12'h6), .Z(constant_cmp_12_5_5_z), .outconst(5'b00100));
  Constant_Cmp_12_5 constant_cmp_12_5_6 (.A(funct), .B(12'h7), .Z(constant_cmp_12_5_6_z), .outconst(5'b00101));
  Constant_Cmp_12_5 constant_cmp_12_5_7 (.A(funct), .B(12'h8), .Z(constant_cmp_12_5_7_z), .outconst(5'b00110));
  Constant_Cmp_12_5 constant_cmp_12_5_8 (.A(funct), .B(12'h9), .Z(constant_cmp_12_5_8_z), .outconst(5'b00111));
  assign and_1_out = constant_cmp_12_5_1_z & bit_extender_1_out;  // AND_Gate and_1, 5 bits wide
  assign and_2_out = constant_cmp_12_5_2_z & bit_extender_1_out;  // AND_Gate and_2, 5 bits wide
  assign and_3_out = constant_cmp_12_5_3_z & bit_extender_1_out;  // AND_Gate and_3, 5 bits wide
  assign and_4_out = constant_cmp_12_5_4_z & bit_extender_1_out;  // AND_Gate and_4, 5 bits wide
  assign and_5_out = constant_cmp_12_5_5_z & bit_extender_1_out;  // AND_Gate and_5, 5 bits wide
  assign and_6_out = constant_cmp_12_5_6_z & bit_extender_1_out;  // AND_Gate and_6, 5 bits wide
  assign and_7_out = constant_cmp_12_5_7_z & bit_extender_1_out;  // AND_Gate and_7, 5 bits wide
  assign and_8_out = constant_cmp_12_5_8_z & bit_extender_1_out;  // AND_Gate and_8, 5 bits wide
  assign or_1_out = and_1_out | and_2_out | and_3_out | and_4_out;  // OR_Gate or_1, 5 bits wide
  assign sel = or_1_out | or_3_out;  // OR_Gate or_2, 5 bits wide
  assign or_3_out = and_5_out | and_6_out | and_7_out | and_8_out;  // OR_Gate or_3, 5 bits wide

  // Notes on the sheet:
  //   Calculates select bit for output mux for R-type math
endmodule

module ALU__RLogic_OB_Selector (
  input  [11:0] opcode,
  input  [11:0] funct,
  output [4:0] sel
);

  wire comparator_1_eq;
  wire [4:0] and_1_out, and_2_out, and_3_out, and_4_out, and_5_out, and_6_out, and_7_out, and_8_out,
       and_9_out, and_10_out, and_11_out, and_12_out, and_13_out, and_14_out, bit_extender_1_out,
       constant_cmp_12_5_1_z, constant_cmp_12_5_2_z, constant_cmp_12_5_3_z, constant_cmp_12_5_4_z,
       constant_cmp_12_5_5_z, constant_cmp_12_5_6_z, constant_cmp_12_5_7_z, constant_cmp_12_5_8_z,
       constant_cmp_12_5_9_z, constant_cmp_12_5_10_z, constant_cmp_12_5_11_z, constant_cmp_12_5_12_z,
       constant_cmp_12_5_13_z, constant_cmp_12_5_14_z, or_1_out, or_2_out;

  Comparator #(.width(12)) comparator_1 (.a(opcode), .b(12'h2), .eq(comparator_1_eq));  // open: gt, lt
  assign bit_extender_1_out = {{4{comparator_1_eq}}, comparator_1_eq};  // Bit_Extender bit_extender_1
  Constant_Cmp_12_5 constant_cmp_12_5_1 (.A(funct), .B({12{1'b0}}), .Z(constant_cmp_12_5_1_z), .outconst(5'b01000));
  Constant_Cmp_12_5 constant_cmp_12_5_2 (.A(funct), .B(12'h1), .Z(constant_cmp_12_5_2_z), .outconst(5'b01001));
  Constant_Cmp_12_5 constant_cmp_12_5_3 (.A(funct), .B(12'h2), .Z(constant_cmp_12_5_3_z), .outconst(5'b01010));
  Constant_Cmp_12_5 constant_cmp_12_5_4 (.A(funct), .B(12'h3), .Z(constant_cmp_12_5_4_z), .outconst(5'b01011));
  Constant_Cmp_12_5 constant_cmp_12_5_5 (.A(funct), .B(12'h4), .Z(constant_cmp_12_5_5_z), .outconst(5'b01100));
  Constant_Cmp_12_5 constant_cmp_12_5_6 (.A(funct), .B(12'h5), .Z(constant_cmp_12_5_6_z), .outconst(5'b01101));
  Constant_Cmp_12_5 constant_cmp_12_5_7 (.A(funct), .B(12'h6), .Z(constant_cmp_12_5_7_z), .outconst(5'b01110));
  Constant_Cmp_12_5 constant_cmp_12_5_8 (.A(funct), .B(12'h8), .Z(constant_cmp_12_5_8_z), .outconst(5'b01111));
  Constant_Cmp_12_5 constant_cmp_12_5_9 (.A(funct), .B(12'h9), .Z(constant_cmp_12_5_9_z), .outconst(5'b10000));
  Constant_Cmp_12_5 constant_cmp_12_5_10 (.A(funct), .B(12'ha), .Z(constant_cmp_12_5_10_z), .outconst(5'b10001));
  Constant_Cmp_12_5 constant_cmp_12_5_11 (.A(funct), .B(12'hb), .Z(constant_cmp_12_5_11_z), .outconst(5'b10010));
  Constant_Cmp_12_5 constant_cmp_12_5_12 (.A(funct), .B(12'hc), .Z(constant_cmp_12_5_12_z), .outconst(5'b10011));
  Constant_Cmp_12_5 constant_cmp_12_5_13 (.A(funct), .B(12'hd), .Z(constant_cmp_12_5_13_z), .outconst(5'b10100));
  Constant_Cmp_12_5 constant_cmp_12_5_14 (.A(funct), .B(12'he), .Z(constant_cmp_12_5_14_z), .outconst(5'b10101));
  assign and_1_out = constant_cmp_12_5_1_z & bit_extender_1_out;  // AND_Gate and_1, 5 bits wide
  assign and_2_out = constant_cmp_12_5_2_z & bit_extender_1_out;  // AND_Gate and_2, 5 bits wide
  assign and_3_out = constant_cmp_12_5_3_z & bit_extender_1_out;  // AND_Gate and_3, 5 bits wide
  assign and_4_out = constant_cmp_12_5_4_z & bit_extender_1_out;  // AND_Gate and_4, 5 bits wide
  assign and_5_out = constant_cmp_12_5_5_z & bit_extender_1_out;  // AND_Gate and_5, 5 bits wide
  assign and_6_out = constant_cmp_12_5_6_z & bit_extender_1_out;  // AND_Gate and_6, 5 bits wide
  assign and_7_out = constant_cmp_12_5_7_z & bit_extender_1_out;  // AND_Gate and_7, 5 bits wide
  assign and_8_out = constant_cmp_12_5_8_z & bit_extender_1_out;  // AND_Gate and_8, 5 bits wide
  assign and_9_out = constant_cmp_12_5_9_z & bit_extender_1_out;  // AND_Gate and_9, 5 bits wide
  assign and_10_out = constant_cmp_12_5_10_z & bit_extender_1_out;  // AND_Gate and_10, 5 bits wide
  assign and_11_out = constant_cmp_12_5_11_z & bit_extender_1_out;  // AND_Gate and_11, 5 bits wide
  assign and_12_out = constant_cmp_12_5_12_z & bit_extender_1_out;  // AND_Gate and_12, 5 bits wide
  assign and_13_out = constant_cmp_12_5_13_z & bit_extender_1_out;  // AND_Gate and_13, 5 bits wide
  assign and_14_out = constant_cmp_12_5_14_z & bit_extender_1_out;  // AND_Gate and_14, 5 bits wide
  assign or_1_out = and_1_out | and_2_out | and_3_out | and_4_out | and_5_out | and_6_out | and_7_out;  // OR_Gate or_1, 5 bits wide
  assign or_2_out = and_8_out | and_9_out | and_10_out | and_11_out | and_12_out | and_13_out | and_14_out;  // OR_Gate or_2, 5 bits wide
  assign sel = or_1_out | or_2_out;  // OR_Gate or_3, 5 bits wide

  // Notes on the sheet:
  //   and
  //   nand
  //   nor
  //   not
  //   or
  //   xnor
  //   xor
  //   land
  //   lnand
  //   lnor
  //   lnot
  //   lor
  //   lxor
  //   lxnor
  //   Calculates select bit for output mux for R-type logic
endmodule

module Double_Cmp_12_1 (
  input  [11:0] X,
  input  [11:0] A,
  input  [11:0] B,
  input  [11:0] Y,
  output Z
);

  wire comparator_1_eq, comparator_2_eq;

  Comparator #(.width(12)) comparator_1 (.a(X), .b(A), .eq(comparator_1_eq));  // open: gt, lt
  and and_1 (Z, comparator_1_eq, comparator_2_eq);
  Comparator #(.width(12)) comparator_2 (.a(B), .b(Y), .eq(comparator_2_eq));  // open: gt, lt
endmodule

module Double_Cmp_12_32 (
  input  [11:0] X,
  input  [11:0] A,
  input  [11:0] B,
  input  [11:0] Y,
  output [31:0] Z
);

  wire and_1_out, comparator_1_eq, comparator_2_eq;

  Comparator #(.width(12)) comparator_1 (.a(X), .b(A), .eq(comparator_1_eq));  // open: gt, lt
  and and_1 (and_1_out, comparator_1_eq, comparator_2_eq);
  Comparator #(.width(12)) comparator_2 (.a(B), .b(Y), .eq(comparator_2_eq));  // open: gt, lt
  assign Z = {{31{and_1_out}}, and_1_out};  // Bit_Extender bit_extender_1
endmodule

module Constant_Cmp_12_5 (
  input  [4:0] outconst,
  input  [11:0] A,
  input  [11:0] B,
  output [4:0] Z
);

  wire comparator_1_eq;
  wire [4:0] bit_extender_1_out;

  Comparator #(.width(12)) comparator_1 (.a(A), .b(B), .eq(comparator_1_eq));  // open: gt, lt
  assign bit_extender_1_out = {{4{comparator_1_eq}}, comparator_1_eq};  // Bit_Extender bit_extender_1
  assign Z = outconst & bit_extender_1_out;  // AND_Gate and_1, 5 bits wide
endmodule
